// Logisim project EP1.circ as structural Verilog: 6 circuits, main circuit main
module main (
  input  OP,
  input  [7:0] Numero_A,
  input  [7:0] Numero_B,
  output [7:0] Resultado,
  output Overflow_C_Sinal,
  output Overflow_S_Sinal
);

  wire somador_1_saida_6, somador_1_saida_7;
  wire [7:0] inversor_1_saida;

  Inversor inversor_1 (.OP(OP), .Numero_B(Numero_B), .Saida(inversor_1_saida));
  Somador somador_1 (
    .OP(OP), .Numero_A(Numero_A), .Numero_B(inversor_1_saida), .Resultado(Resultado),
    .Saida_6(somador_1_saida_6), .Saida_7(somador_1_saida_7));
  Overflow_com_Sinal overflow_com_sinal_1 (
    .OP(OP), .BIT_6(somador_1_saida_6), .BIT_7(somador_1_saida_7), .Saida(Overflow_C_Sinal));
  Overflow_sem_Sinal overflow_sem_sinal_1 (
    .OP(OP), .BIT_6(somador_1_saida_6), .BIT_7(somador_1_saida_7), .Saida(Overflow_S_Sinal));

  // Notes on the sheet:
  //   Circuito_Somador
endmodule

module Somabits (
  input  OP,
  input  BIT_A,
  input  BIT_B,
  output Unidade,
  output Vai_Um
);

  wire and_1_out, and_2_out, and_3_out, and_4_out, and_5_out, and_6_out, and_7_out, and_8_out, and_9_out,
       and_10_out, and_11_out, and_12_out, and_13_out, and_14_out, and_15_out, and_16_out, not_1_out,
       not_2_out, not_3_out, xor_1_out, xor_2_out, xor_3_out, xor_4_out;

  not not_1 (not_1_out, OP);
  not not_2 (not_2_out, BIT_A);
  not not_3 (not_3_out, BIT_B);
  and and_1 (and_1_out, not_1_out, not_2_out);
  and and_2 (and_2_out, not_1_out, BIT_A);
  and and_3 (and_3_out, OP, not_2_out);
  and and_4 (and_4_out, OP, BIT_A);
  and and_5 (and_5_out, not_1_out, BIT_A);
  and and_6 (and_6_out, OP, not_2_out);
  and and_7 (and_7_out, OP, BIT_A);
  and and_8 (and_8_out, OP, BIT_A);
  and and_9 (and_9_out, and_1_out, BIT_B);
  and and_10 (and_10_out, and_2_out, not_3_out);
  and and_11 (and_11_out, and_3_out, not_3_out);
  and and_12 (and_12_out, and_4_out, BIT_B);
  and and_13 (and_13_out, and_5_out, BIT_B);
  and and_14 (and_14_out, and_6_out, BIT_B);
  and and_15 (and_15_out, and_7_out, not_3_out);
  and and_16 (and_16_out, and_8_out, BIT_B);
  xor xor_1 (xor_1_out, and_9_out, and_10_out);
  xor xor_2 (xor_2_out, and_11_out, and_12_out);
  xor xor_3 (xor_3_out, and_13_out, and_14_out);
  xor xor_4 (xor_4_out, and_15_out, and_16_out);
  xor xor_5 (Unidade, xor_1_out, xor_2_out);
  xor xor_6 (Vai_Um, xor_3_out, xor_4_out);
endmodule

module Somador (
  input  OP,
  input  [7:0] Numero_A,
  input  [7:0] Numero_B,
  output [7:0] Resultado,
  output Saida_6,
  output Saida_7
);

  wire somabits_1_vai_um, somabits_2_vai_um, somabits_3_vai_um, somabits_4_vai_um, somabits_5_vai_um,
       somabits_6_vai_um;

  Somabits somabits_1 (
    .OP(OP), .BIT_A(Numero_A[0]), .BIT_B(Numero_B[0]), .Unidade(Resultado[0]), .Vai_Um(somabits_1_vai_um));
  Somabits somabits_2 (
    .OP(somabits_1_vai_um), .BIT_A(Numero_A[1]), .BIT_B(Numero_B[1]), .Unidade(Resultado[1]),
    .Vai_Um(somabits_2_vai_um));
  Somabits somabits_3 (
    .OP(somabits_2_vai_um), .BIT_A(Numero_A[2]), .BIT_B(Numero_B[2]), .Unidade(Resultado[2]),
    .Vai_Um(somabits_3_vai_um));
  Somabits somabits_4 (
    .OP(somabits_3_vai_um), .BIT_A(Numero_A[3]), .BIT_B(Numero_B[3]), .Unidade(Resultado[3]),
    .Vai_Um(somabits_4_vai_um));
  Somabits somabits_5 (
    .OP(somabits_4_vai_um), .BIT_A(Numero_A[4]), .BIT_B(Numero_B[4]), .Unidade(Resultado[4]),
    .Vai_Um(somabits_5_vai_um));
  Somabits somabits_6 (
    .OP(somabits_5_vai_um), .BIT_A(Numero_A[5]), .BIT_B(Numero_B[5]), .Unidade(Resultado[5]),
    .Vai_Um(somabits_6_vai_um));
  Somabits somabits_7 (
    .OP(somabits_6_vai_um), .BIT_A(Numero_A[6]), .BIT_B(Numero_B[6]), .Unidade(Resultado[6]), .Vai_Um(Saida_6));
  Somabits somabits_8 (
    .OP(Saida_6), .BIT_A(Numero_A[7]), .BIT_B(Numero_B[7]), .Unidade(Resultado[7]), .Vai_Um(Saida_7));
endmodule

module Overflow_com_Sinal (
  input  OP,
  input  BIT_6,
  input  BIT_7,
  output Saida
);

  wire and_1_out, and_2_out, and_3_out, and_4_out, and_5_out, and_6_out, and_7_out, and_8_out, not_1_out,
       not_2_out, not_3_out, xor_1_out, xor_2_out;

  not not_1 (not_1_out, OP);
  not not_2 (not_2_out, BIT_6);
  not not_3 (not_3_out, BIT_7);
  and and_1 (and_1_out, OP, not_2_out);
  and and_2 (and_2_out, OP, BIT_6);
  and and_3 (and_3_out, not_1_out, not_2_out);
  and and_4 (and_4_out, not_1_out, BIT_6);
  and and_5 (and_5_out, and_1_out, BIT_7);
  and and_6 (and_6_out, and_2_out, not_3_out);
  and and_7 (and_7_out, and_3_out, BIT_7);
  and and_8 (and_8_out, and_4_out, not_3_out);
  xor xor_1 (xor_1_out, and_5_out, and_6_out);
  xor xor_2 (xor_2_out, and_7_out, and_8_out);
  xor xor_3 (Saida, xor_1_out, xor_2_out);
endmodule

module Overflow_sem_Sinal (
  input  OP,
  input  BIT_6,
  input  BIT_7,
  output Saida
);

  wire and_1_out, and_2_out, and_3_out, and_4_out, and_5_out, and_6_out, and_7_out, and_8_out, not_1_out,
       not_2_out, not_3_out, xor_1_out, xor_2_out;

  not not_1 (not_1_out, OP);
  not not_2 (not_2_out, BIT_6);
  not not_3 (not_3_out, BIT_7);
  and and_1 (and_1_out, OP, BIT_6);
  and and_2 (and_2_out, OP, not_2_out);
  and and_3 (and_3_out, not_1_out, BIT_6);
  and and_4 (and_4_out, not_1_out, not_2_out);
  and and_5 (and_5_out, and_1_out, not_3_out);
  and and_6 (and_6_out, and_2_out, not_3_out);
  and and_7 (and_7_out, and_3_out, BIT_7);
  and and_8 (and_8_out, and_4_out, BIT_7);
  xor xor_1 (xor_1_out, and_5_out, and_6_out);
  xor xor_2 (xor_2_out, and_7_out, and_8_out);
  xor xor_3 (Saida, xor_1_out, xor_2_out);
endmodule

module Inversor (
  input  OP,
  input  [7:0] Numero_B,
  output [7:0] Saida
);

  xor xor_1 (Saida[0], OP, Numero_B[0]);
  xor xor_2 (Saida[1], OP, Numero_B[1]);
  xor xor_3 (Saida[2], OP, Numero_B[2]);
  xor xor_4 (Saida[3], OP, Numero_B[3]);
  xor xor_5 (Saida[4], OP, Numero_B[4]);
  xor xor_6 (Saida[5], OP, Numero_B[5]);
  xor xor_7 (Saida[6], OP, Numero_B[6]);
  xor xor_8 (Saida[7], OP, Numero_B[7]);
endmodule
