// Logisim project EP3.circ as structural Verilog: 20 circuits, main circuit Comparabits
module Main (
  input  [7:0] in_1,
  output [7:0] out_2
);

  Processador processador_1 (.Entrada_Processador(in_1), .Saida_Processador(out_2));

  // Notes on the sheet:
  //   NUSP: 14600541
  //   Nathália Yukimi Uchiyama Tsuno
endmodule

module Processador (
  input  [7:0] Entrada_Processador,
  output [7:0] Saida_Processador
);

  wire clock_1_out, ED, pc_1_we_ram, S0, S1, S2, S3, S4, S7, S8, S9, SA;
  wire [7:0] EE, pc_1_saida, Saida_AC;
  wire [15:0] pc_1_saida_habilitador, ram_1_dout, Saida_IR;

  PC pc_1 (
    .Entrada(Entrada_Processador), .AC(Saida_AC), .EE(EE), .S0(S0), .S1(S1), .S2(S2), .S3(S3), .S4(S4),
    .S7(S7), .S8(S8), .S9(S9), .SA(SA), .Entrada_Destinador(ED), .Saida_habilitador(pc_1_saida_habilitador),
    .Saida(pc_1_saida), .WE_RAM(pc_1_we_ram));
  RAM #(.asyncread("true"), .dataWidth(16)) ram_1 (
    .addr(pc_1_saida), .we(pc_1_we_ram), .clk(clock_1_out), .din(pc_1_saida_habilitador), .dout(ram_1_dout));  // open: oe
  Clock clock_1 (.out(clock_1_out));
  CPU cpu_1 (
    .Entrada_CPU(Saida_IR), .Saida_AC(Saida_AC), .EE(EE), .S0(S0), .S1(S1), .S2(S2), .S3(S3), .S4(S4),
    .S7(S7), .S8(S8), .S9(S9), .SA(SA), .Saida_Destinador(ED));
  Saida saida_1 (.EE(EE), .S8(S8), .Saida_Processador(Saida_Processador));
  IR ir_1 (.in_1(ram_1_dout), .S9(S9), .out_3(Saida_IR));

  // Other names for the same wires on the sheet: Entrada[7:0] = Entrada_Processador
endmodule

module CPU (
  input  [15:0] Entrada_CPU,
  output [7:0] Saida_AC,
  output [7:0] EE,
  output S0,
  output S1,
  output S2,
  output S3,
  output S4,
  output S7,
  output S8,
  output S9,
  output SA,
  output Saida_Destinador
);

  wire C3, C4, C5, clock_1_out, or_1_out, register_1_q, SB, SD, SF;
  wire [7:0] multiplexer_1_out, Resultado, zero_1_saida;

  Clock clock_1 (.out(clock_1_out));
  Register #(.width(1)) register_1 (.D(S4), .en(clock_1_out), .clk(clock_1_out), .Q(register_1_q));  // open: clr
  or or_1 (or_1_out, SB, SD, SF);
  Multiplexer #(.width(8)) multiplexer_1 (.in0(EE), .in1(zero_1_saida), .out(multiplexer_1_out), .sel(or_1_out));
  Zero zero_1 (.Entrada(S0), .Saida(zero_1_saida));
  ULA ula_1 (
    .Controle(register_1_q), .A(Saida_AC), .B(multiplexer_1_out), .C3(C3), .C4(C4), .C5(C5),
    .Resultado(Resultado));  // open: Overflow_Sem_Sinal, Overflow_Com_Sinal, C0, C1, C2
  UC uc_1 (
    .in_1(Entrada_CPU), .EE(EE), .S0(S0), .S1(S1), .S2(S2), .S3(S3), .S4(S4), .S7(S7), .S8(S8), .S9(S9),
    .SA(SA), .SB(SB), .SD(SD), .SF(SF));
  AC ac_1 (.EE(EE), .Resultado(Resultado), .S1(S1), .S3(S3), .S4(S4), .S9(S9), .Saida_AC(Saida_AC));
  Destinador destinador_1 (.C3(C3), .SD(SD), .C4(C4), .SB(SB), .C5(C5), .SF(SF), .Saida_Destinador(Saida_Destinador));
endmodule

module ULA (
  input  Controle,
  input  [7:0] A,
  input  [7:0] B,
  output Overflow_Sem_Sinal,
  output Overflow_Com_Sinal,
  output C0,
  output C1,
  output C2,
  output C3,
  output C4,
  output C5,
  output [7:0] Resultado
);

  wire somador_1_carry_6, somador_1_carry_7;
  wire [7:0] inversor_de_sinal_1_numero_barrado;

  Inversor_de_Sinal inversor_de_sinal_1 (
    .OP(Controle), .Numero(B), .Numero_barrado(inversor_de_sinal_1_numero_barrado));
  Somador somador_1 (
    .OP(Controle), .A(A), .B(inversor_de_sinal_1_numero_barrado), .Resultado(Resultado),
    .Carry_6(somador_1_carry_6), .Carry_7(somador_1_carry_7));
  Comparador comparador_1 (.A(A), .B(B), .C0(C0), .C1(C1), .C2(C2), .C3(C3), .C4(C4), .C5(C5));
  xor xor_1 (Overflow_Sem_Sinal, Controle, somador_1_carry_7);
  xor xor_2 (Overflow_Com_Sinal, somador_1_carry_6, somador_1_carry_7);

  // Notes on the sheet:
  //   A > B 
  //   A < B
  //   A == B
  //   A == 0
  //   A > B (Considerando o Sinal)
  //   A < B (Considerando o Sinal)
endmodule

module UC (
  input  [15:0] in_1,
  output [7:0] EE,
  output S0,
  output S1,
  output S2,
  output S3,
  output S4,
  output S7,
  output S8,
  output S9,
  output SA,
  output SB,
  output SD,
  output SF
);

  wire nor_1_out;

  nor nor_1 (nor_1_out, in_1[12], in_1[13], in_1[14], in_1[15]);
  Demultiplexer #(.select(4)) demultiplexer_1 (
    .out0(S0), .out1(S1), .out2(S2), .out3(S3), .out4(S4), .out7(S7), .out8(S8), .out9(S9), .out10(SA),
    .out11(SB), .out13(SD), .out15(SF), .in(nor_1_out), .sel(in_1[11:8]));  // open: out5, out6, out12, out14

  assign EE = in_1[7:0];
endmodule

module Comparabits (
  input  Controle,
  input  digito_a,
  input  digito_b,
  output out_4,
  output out_5,
  output out_6
);

  wire not_1_out, not_2_out, not_3_out, xor_1_out;

  xor xor_1 (xor_1_out, digito_a, digito_b);
  not not_1 (not_1_out, xor_1_out);
  not not_2 (not_2_out, digito_a);
  not not_3 (not_3_out, digito_b);
  and and_1 (out_4, Controle, not_1_out);
  and and_2 (out_5, not_2_out, Controle, digito_b);
  and and_3 (out_6, digito_a, Controle, not_3_out);

  // Notes on the sheet:
  //   digito_a = digito_b
  //   digito_a < digito_b
  //   digito_a > digito_b
endmodule

module Circuito_Comparador (
  input  Controle,
  input  [7:0] A,
  input  [7:0] B,
  output out_4,
  output out_5,
  output out_6
);

  wire comparabits0_out_4, comparabits0_out_5, comparabits0_out_6, comparabits1_out_4, comparabits1_out_5,
       comparabits1_out_6, comparabits2_out_4, comparabits2_out_5, comparabits2_out_6, comparabits3_out_4,
       comparabits3_out_5, comparabits3_out_6, comparabits4_out_4, comparabits4_out_5, comparabits4_out_6,
       comparabits5_out_4, comparabits5_out_5, comparabits5_out_6, comparabits6_out_4, comparabits6_out_5,
       comparabits6_out_6, comparabits7_out_5, comparabits7_out_6;

  Comparabits comparabits0 (
    .Controle(Controle), .digito_a(A[7]), .digito_b(B[7]), .out_4(comparabits0_out_4),
    .out_5(comparabits0_out_5), .out_6(comparabits0_out_6));
  Comparabits comparabits1 (
    .Controle(comparabits0_out_4), .digito_a(A[6]), .digito_b(B[6]), .out_4(comparabits1_out_4),
    .out_5(comparabits1_out_5), .out_6(comparabits1_out_6));
  Comparabits comparabits2 (
    .Controle(comparabits1_out_4), .digito_a(A[5]), .digito_b(B[5]), .out_4(comparabits2_out_4),
    .out_5(comparabits2_out_5), .out_6(comparabits2_out_6));
  Comparabits comparabits3 (
    .Controle(comparabits2_out_4), .digito_a(A[4]), .digito_b(B[4]), .out_4(comparabits3_out_4),
    .out_5(comparabits3_out_5), .out_6(comparabits3_out_6));
  Comparabits comparabits4 (
    .Controle(comparabits3_out_4), .digito_a(A[3]), .digito_b(B[3]), .out_4(comparabits4_out_4),
    .out_5(comparabits4_out_5), .out_6(comparabits4_out_6));
  Comparabits comparabits5 (
    .Controle(comparabits4_out_4), .digito_a(A[2]), .digito_b(B[2]), .out_4(comparabits5_out_4),
    .out_5(comparabits5_out_5), .out_6(comparabits5_out_6));
  Comparabits comparabits6 (
    .Controle(comparabits5_out_4), .digito_a(A[1]), .digito_b(B[1]), .out_4(comparabits6_out_4),
    .out_5(comparabits6_out_5), .out_6(comparabits6_out_6));
  Comparabits comparabits7 (
    .Controle(comparabits6_out_4), .digito_a(A[0]), .digito_b(B[0]), .out_4(out_6),
    .out_5(comparabits7_out_5), .out_6(comparabits7_out_6));
  or or_1 (out_4, comparabits0_out_5, comparabits1_out_5, comparabits2_out_5, comparabits3_out_5, comparabits4_out_5, comparabits5_out_5, comparabits6_out_5, comparabits7_out_5);
  or or_2 (out_5, comparabits0_out_6, comparabits1_out_6, comparabits2_out_6, comparabits3_out_6, comparabits4_out_6, comparabits5_out_6, comparabits6_out_6, comparabits7_out_6);

  // Notes on the sheet:
  //   A < B
  //   A > B
  //   A == B
endmodule

module Comparador (
  input  [7:0] A,
  input  [7:0] B,
  output C0,
  output C1,
  output C2,
  output C3,
  output C4,
  output C5
);

  wire circuito_comparador_1_out_4, circuito_comparador_1_out_5, verifica_sinal_1_out_3,
       verifica_sinal_1_out_4, verifica_sinal_1_out_5;

  Verifica_Sinal verifica_sinal_1 (
    .digito_a(A[7]), .digito_b(B[7]), .out_3(verifica_sinal_1_out_3), .out_4(verifica_sinal_1_out_4),
    .out_5(verifica_sinal_1_out_5));
  Circuito_Comparador circuito_comparador_1 (
    .Controle(verifica_sinal_1_out_3), .A(A), .B(B), .out_4(circuito_comparador_1_out_4),
    .out_5(circuito_comparador_1_out_5), .out_6(C2));
  nor nor_1 (C3, A[0], A[1], A[2], A[3], A[4], A[5], A[6], A[7]);
  xor xor_1 (C0, circuito_comparador_1_out_5, verifica_sinal_1_out_5);
  xor xor_2 (C1, circuito_comparador_1_out_4, verifica_sinal_1_out_4);
  xor xor_3 (C4, circuito_comparador_1_out_5, verifica_sinal_1_out_4);
  xor xor_4 (C5, circuito_comparador_1_out_4, verifica_sinal_1_out_5);
endmodule

module Verifica_Sinal (
  input  digito_a,
  input  digito_b,
  output out_3,
  output out_4,
  output out_5
);

  wire not_1_out, not_2_out, xor_1_out;

  not not_1 (not_1_out, digito_a);
  not not_2 (not_2_out, digito_b);
  xor xor_1 (xor_1_out, digito_a, digito_b);
  and and_1 (out_4, not_1_out, digito_b);
  and and_2 (out_5, digito_a, not_2_out);
  not not_3 (out_3, xor_1_out);

  // Notes on the sheet:
  //   digito_a = digito_b
  //   digito_a < digito_b
  //   digito_a > digito_b
endmodule

module Somabits (
  input  carry_in,
  input  digito_a,
  input  digito_b,
  output s,
  output carry_out
);

  wire and_1_out, and_2_out, and_3_out, and_4_out, not_1_out, xnor_1_out, xor_1_out;

  not not_1 (not_1_out, carry_in);
  xor xor_1 (xor_1_out, digito_a, digito_b);
  xnor xnor_1 (xnor_1_out, digito_a, digito_b);
  and and_1 (and_1_out, not_1_out, xor_1_out);
  and and_2 (and_2_out, carry_in, xnor_1_out);
  and and_3 (and_3_out, carry_in, xor_1_out);
  and and_4 (and_4_out, digito_a, digito_b);
  or or_1 (s, and_1_out, and_2_out);
  or or_2 (carry_out, and_3_out, and_4_out);
endmodule

module Somador (
  input  OP,
  input  [7:0] A,
  input  [7:0] B,
  output [7:0] Resultado,
  output Carry_6,
  output Carry_7
);

  wire somabits_1_carry_out, somabits_2_carry_out, somabits_3_carry_out, somabits_4_carry_out,
       somabits_5_carry_out, somabits_6_carry_out;

  Somabits somabits_1 (
    .carry_in(OP), .digito_a(A[0]), .digito_b(B[0]), .s(Resultado[0]), .carry_out(somabits_1_carry_out));
  Somabits somabits_2 (
    .carry_in(somabits_1_carry_out), .digito_a(A[1]), .digito_b(B[1]), .s(Resultado[1]),
    .carry_out(somabits_2_carry_out));
  Somabits somabits_3 (
    .carry_in(somabits_2_carry_out), .digito_a(A[2]), .digito_b(B[2]), .s(Resultado[2]),
    .carry_out(somabits_3_carry_out));
  Somabits somabits_4 (
    .carry_in(somabits_3_carry_out), .digito_a(A[3]), .digito_b(B[3]), .s(Resultado[3]),
    .carry_out(somabits_4_carry_out));
  Somabits somabits_5 (
    .carry_in(somabits_4_carry_out), .digito_a(A[4]), .digito_b(B[4]), .s(Resultado[4]),
    .carry_out(somabits_5_carry_out));
  Somabits somabits_6 (
    .carry_in(somabits_5_carry_out), .digito_a(A[5]), .digito_b(B[5]), .s(Resultado[5]),
    .carry_out(somabits_6_carry_out));
  Somabits somabits_7 (
    .carry_in(somabits_6_carry_out), .digito_a(A[6]), .digito_b(B[6]), .s(Resultado[6]), .carry_out(Carry_6));
  Somabits somabits_8 (.carry_in(Carry_6), .digito_a(A[7]), .digito_b(B[7]), .s(Resultado[7]), .carry_out(Carry_7));
endmodule

module Inversor_de_Sinal (
  input  OP,
  input  [7:0] Numero,
  output [7:0] Numero_barrado
);

  xor xor_1 (Numero_barrado[0], OP, Numero[0]);
  xor xor_2 (Numero_barrado[1], OP, Numero[1]);
  xor xor_3 (Numero_barrado[2], OP, Numero[2]);
  xor xor_4 (Numero_barrado[3], OP, Numero[3]);
  xor xor_5 (Numero_barrado[4], OP, Numero[4]);
  xor xor_6 (Numero_barrado[5], OP, Numero[5]);
  xor xor_7 (Numero_barrado[6], OP, Numero[6]);
  xor xor_8 (Numero_barrado[7], OP, Numero[7]);
endmodule

module IR (
  input  [15:0] in_1,
  input  S9,
  output [15:0] out_3
);

  wire clock_1_out, not_1_out, register_1_q;

  Clock clock_1 (.out(clock_1_out));
  not not_1 (not_1_out, register_1_q);
  Register #(.width(1)) register_1 (.D(S9), .en(S9), .clk(clock_1_out), .Q(register_1_q));  // open: clr
  Register #(.width(16)) register_2 (.D(in_1), .en(not_1_out), .clk(clock_1_out), .Q(out_3), .clr(register_1_q));
endmodule

module AC (
  input  [7:0] EE,
  input  [7:0] Resultado,
  input  S1,
  input  S3,
  input  S4,
  input  S9,
  output [7:0] Saida_AC
);

  wire clock_1_out, or_1_out, or_2_out, or_3_out, register_1_q, register_2_q, register_3_q;
  wire [7:0] multiplexer_1_out;

  Clock clock_1 (.out(clock_1_out));
  Register #(.width(1)) register_1 (.D(S1), .en(clock_1_out), .clk(clock_1_out), .Q(register_1_q));  // open: clr
  Register #(.width(1)) register_2 (.D(or_1_out), .en(clock_1_out), .clk(clock_1_out), .Q(register_2_q));  // open: clr
  or or_1 (or_1_out, S3, S4);
  Register #(.width(1)) register_3 (.D(S9), .en(S9), .clk(clock_1_out), .Q(register_3_q));  // open: clr
  or or_2 (or_2_out, register_1_q, register_2_q);
  Multiplexer #(.width(8)) multiplexer_1 (.in0(EE), .in1(Resultado), .out(multiplexer_1_out), .sel(register_2_q));
  Register register_4 (.D(multiplexer_1_out), .en(or_2_out), .clk(clock_1_out), .Q(Saida_AC), .clr(or_3_out));
  or or_3 (or_3_out, S9, register_3_q);
endmodule

module PC (
  input  [7:0] Entrada,
  input  [7:0] AC,
  input  [7:0] EE,
  input  S0,
  input  S1,
  input  S2,
  input  S3,
  input  S4,
  input  S7,
  input  S8,
  input  S9,
  input  SA,
  input  Entrada_Destinador,
  output [15:0] Saida_habilitador,
  output [7:0] Saida,
  output WE_RAM
);

  wire clock_1_out, not_1_out, or_1_out, or_2_out, or_3_out, register_1_q;
  wire [7:0] multiplexer_1_out, register_2_q, somador_1_resultado, um_1_out_2;

  Clock clock_1 (.out(clock_1_out));
  or or_1 (or_1_out, SA, Entrada_Destinador);
  or or_2 (or_2_out, S1, S2, S3, S4, S7, S8);
  Register #(.width(1)) register_1 (.D(S9), .en(S9), .clk(clock_1_out), .Q(register_1_q));  // open: clr
  Register register_2 (.D(somador_1_resultado), .en(not_1_out), .clk(clock_1_out), .Q(register_2_q), .clr(or_3_out));
  not not_1 (not_1_out, or_2_out);
  or or_3 (or_3_out, S9, register_1_q);
  Multiplexer #(.width(8)) multiplexer_1 (.in0(register_2_q), .in1(EE), .out(multiplexer_1_out), .sel(or_1_out));
  Um um_1 (.in_1(S0), .out_2(um_1_out_2));
  Multiplexer #(.width(8)) multiplexer_2 (.in0(multiplexer_1_out), .in1(EE), .out(Saida), .sel(or_2_out));
  Somador somador_1 (
    .A(um_1_out_2), .B(multiplexer_1_out), .Resultado(somador_1_resultado));  // open: OP, Carry_6, Carry_7
  or or_4 (WE_RAM, S2, S7);
  Habilitador habilitador_1 (.AC(AC), .Entrada(Entrada), .S0(S0), .S7(S7), .Saida(Saida_habilitador));
endmodule

module Habilitador (
  input  [7:0] AC,
  input  [7:0] Entrada,
  input  S0,
  input  S7,
  output [15:0] Saida
);

  Multiplexer #(.width(8)) multiplexer_1 (.in0(AC), .in1(Entrada), .out(Saida[7:0]), .sel(S7));
  Zero zero_1 (.Entrada(S0), .Saida(Saida[15:8]));
endmodule

module Zero (
  input  Entrada,
  output [7:0] Saida
);


  assign Saida = {8{Entrada}};

  // Other names for the same wires on the sheet: Zero = Entrada
endmodule

module Um (
  input  in_1,
  output [7:0] out_2
);

  wire not_1_out;

  not not_1 (not_1_out, in_1);
  not not_2 (out_2[0], out_2[7]);
  and and_1 (out_2[7], in_1, not_1_out);

  assign out_2[6:1] = {6{out_2[7]}};

  // Other names for the same wires on the sheet: Um = out_2[7]
endmodule

module Saida (
  input  [7:0] EE,
  input  S8,
  output [7:0] Saida_Processador
);

  wire clock_1_out, register_1_q;

  Clock clock_1 (.out(clock_1_out));
  Register #(.width(1)) register_1 (.D(S8), .en(clock_1_out), .clk(clock_1_out), .Q(register_1_q));  // open: clr
  Register register_2 (.D(EE), .en(register_1_q), .clk(clock_1_out), .Q(Saida_Processador));  // open: clr
endmodule

module Destinador (
  input  C3,
  input  SD,
  input  C4,
  input  SB,
  input  C5,
  input  SF,
  output Saida_Destinador
);

  wire multiplexer_1_out, multiplexer_2_out, multiplexer_3_out;

  Multiplexer multiplexer_1 (.in0(SD), .in1(C3), .out(multiplexer_1_out), .sel(SD));
  Multiplexer multiplexer_2 (.in0(SB), .in1(C4), .out(multiplexer_2_out), .sel(SB));
  Multiplexer multiplexer_3 (.in0(SF), .in1(C5), .out(multiplexer_3_out), .sel(SF));
  or or_1 (Saida_Destinador, multiplexer_1_out, multiplexer_2_out, multiplexer_3_out);
endmodule
